# Fritzing sketch Project (saved by Fritzing 0.9.3b)
breadboards: 1

parts:
  R1 = Resistor [tolerance=±20% resistance=10k package=THT]
  C1 = Electrolytic Capacitor [capacitance=1µF package="100 mil [THT, electrolytic]"]
  Part1 = Arduino Uno (Rev3)
  D1 = Rectifier Diode [part_number=1N4001 package="300 mil [THT]"]
  T1 = LM35 Temperature Sensor [package="TO92 [THT]"]
  LED1 = smd LED [color="Yellow (585nm)" package="0805 [SMD]"]  # not connected
  LED2 = smd LED [color="White (6500K)" package="0805 [SMD]"]  # not connected
  LED3 = smd LED [color="Green (560nm)" package="0805 [SMD]"]  # not connected
  R2 = Resistor [tolerance=±5% resistance=220 package="2010 [SMD]"]
  R3 = Resistor [tolerance=±5% resistance=220 package="2010 [SMD]"]
  R4 = Resistor [tolerance=±5% resistance=220 package="2010 [SMD]"]
  F1 = Fan - Ventilador [package=THT]
  Q1 = PNP-Transistor [package="TO92 [THT]"]

nets:
  N1: R1.Pin_0, C1.+, D1.cathode, Q1.C
  GND: R1.Pin_1, Part1.GND, T1.GND
  N2: C1.-, F1.GND, Q1.B
  N3: Part1.A1, T1.Vout
  N4: Part1.D8, R2.Pin_0, R2.Pin_1
  N5: Part1.D11_PWM/MOSI, Q1.E
  N6: Part1.D5_PWM, R3.Pin_0, R3.Pin_1
  N7: Part1.D7, R4.Pin_0, R4.Pin_1
  N8: Part1.5V, T1.+Vs
  N9: D1.anode, F1.5V

custom parts:
  Fan - Ventilador: Ventilador de 2 pines, se encuentra comunmente en computadoras de escritorio
